# Fritzing sketch esp_lm75 (saved by Fritzing 0.9.3b)
breadboards: 1

parts:
  U1 = ESP8266 WiFi Module [part_number=ESP8266]
  Part1 = Arduino Uno (Rev3) - ICSP
  R1 = Resistor [tolerance=±5% resistance=220 package="0402 [SMD]"]

nets:
  N1: U1.RXD, Part1.D10_PWM/SS
  VCC: U1.VCC, Part1.3V3, R1.Pin_0
  N2: U1.RST, Part1.RESET
  N3: U1.CH_PD, R1.Pin_1
  GND: U1.GND, Part1.GND
  N4: U1.TXD, Part1.D9_PWM

custom parts:
  ESP8266 WiFi Module: Generic WiFi Module based on the ESP8266 with onboard PCB antenna and UART communications
